// Digital circuit misa.dig as structural Verilog
module misa (
  input  in_1,
  input  in_2,
  input  in_3,
  input  [3:0] in_4,
  input  [3:0] in_5,
  input  [3:0] in_6,
  input  [7:0] in_8,
  output [7:0] out_7
);

  regfile regfile_1 (
    .reg__port1(in_6), .reg__port2(in_5), .reg__port3(in_4), .reg__port1__write(in_3),
    .reg__port2__write(in_2), .reg__clk(in_1), .reg__port1__data(out_7));  // open: reg__port2__data, reg__port3__data
  assign out_7 = in_3 ? in_8 : 8'bz;  // Driver driver_1
endmodule
